# Fritzing sketch 01.sonic_car_아두이노전원_가로 (saved by Fritzing 0.9.3b)
breadboards: 1

parts:
  부품1 = Arduino Uno (Rev3)
  U1 = L9110 H-bridge module [part_number="L9110 H-bridge"]
  M1 = DC Motor
  M2 = DC Motor
  HC-SR04_Sensor_1 = HC-SR04 Ultrasonic Distance Sensor
  VCC2 = 4 x AAA Battery Mount

nets:
  N1: 부품1.A0, HC-SR04_Sensor_1.TRIG
  N2: 부품1.A1, HC-SR04_Sensor_1.ECHO
  N3: 부품1.D9_PWM, U1.B-IB
  N4: 부품1.D10_PWM/SS, U1.B-IA
  N5: 부품1.D5_PWM, U1.A-IB
  N6: 부품1.D6_PWM, U1.A-IA
  5V: 부품1.5V, HC-SR04_Sensor_1.VCC
  GND: 부품1.GND, U1.GND, HC-SR04_Sensor_1.GND, VCC2.-
  N7: U1.VCC, VCC2.+
  N8: U1.MOTOR_A-A, M2.pin_1
  N9: U1.MOTOR_A-B, M2.pin_2
  N10: U1.MOTOR_B-A, M1.pin_2
  N11: U1.MOTOR_B-B, M1.pin_1
