# Fritzing sketch 01.sonic_mpu6050_car_아두이노전원 (saved by Fritzing 0.9.3b)
breadboards: 1

parts:
  부품1 = Arduino Uno (Rev3)
  U1 = L9110 H-bridge module [part_number="L9110 H-bridge"]
  M1 = DC Motor
  M2 = DC Motor
  HC-SR04_Sensor_1 = HC-SR04 Ultrasonic Distance Sensor
  VCC2 = 4 x AAA Battery Mount
  부품2 = InvenSense MPU6050

nets:
  N1: 부품1.A0, HC-SR04_Sensor_1.TRIG
  N2: 부품1.A1, HC-SR04_Sensor_1.ECHO
  N3: 부품1.A4/SDA, 부품2.SDA
  N4: 부품1.A5/SCL, 부품2.SCL
  N5: 부품1.D9_PWM, U1.B-IB
  N6: 부품1.D10_PWM/SS, U1.B-IA
  N7: 부품1.D2, 부품2.INT
  N8: 부품1.D5_PWM, U1.A-IB
  N9: 부품1.D6_PWM, U1.A-IA
  VCC: 부품1.5V, HC-SR04_Sensor_1.VCC, 부품2.VCC
  GND: 부품1.GND, U1.GND, HC-SR04_Sensor_1.GND, VCC2.-, 부품2.GND
  N10: U1.VCC, VCC2.+
  N11: U1.MOTOR_A-A, M2.pin_1
  N12: U1.MOTOR_A-B, M2.pin_2
  N13: U1.MOTOR_B-A, M1.pin_2
  N14: U1.MOTOR_B-B, M1.pin_1
